# Fritzing sketch BioHackHeater (saved by Fritzing 0.9.2b)
breadboards: 1

parts:
  Part1 = Arduino Uno (Rev3)
  U1 = RELAY-SOLIDSTATE [package=relay-s108t02]
  T1 = LM35 Temperature Sensor [package="TO92 [THT]"]
  R1 = 10 kΩ Resistor [package=THT]
  R2 = 10 kΩ Resistor [package=THT]

nets:
  N1: Part1.A0, Part1.5V, R1.Pin_1, R2.Pin_0
  N2: Part1.A1, T1.+Vs, R1.Pin_0
  N3: Part1.D13/SCK, U1.+
  GND: Part1.GND, U1.-, T1.GND
  N4: Part1.D2, R2.Pin_1

custom parts:
  10 kΩ Resistor: A generic resistor (0.25W)
